# Fritzing sketch POV Base Simples Arduino (saved by Fritzing 0.7.11b)

parts:
  R1 = Photocell (LDR) [package=THT]
  R2 = Resistor [tolerance=±5% resistance=220 package=THT]
  R3 = Resistor [tolerance=±5% resistance=220 package=THT]
  R4 = Resistor [tolerance=±5% resistance=220 package=THT]
  R5 = Resistor [tolerance=±5% resistance=220 package=THT]
  R6 = Resistor [tolerance=±5% resistance=220 package=THT]
  R7 = Resistor [tolerance=±5% resistance=220 package=THT]
  LED1 = LED - 5mm [color="White (8000K)" package="5 mm [THT]"]
  LED3 = LED - 5mm [color="White (8000K)" package="5 mm [THT]"]
  LED4 = LED - 5mm [color="White (8000K)" package="5 mm [THT]"]
  LED5 = LED - 5mm [color="White (8000K)" package="5 mm [THT]"]
  LED6 = LED - 5mm [color="White (8000K)" package="5 mm [THT]"]
  LED7 = LED - 5mm [color="White (8000K)" package="5 mm [THT]"]
  R8 = Resistor [tolerance=±5% resistance=220 package=THT]
  LED8 = LED - 5mm [color="White (8000K)" package="5 mm [THT]"]
  R9 = Resistor [tolerance=±5% resistance=220 package=THT]
  LED9 = LED - 5mm [color="White (8000K)" package="5 mm [THT]"]
  DC_Power1 = DC Power [voltage=5]
  J10 = Generic female header - metal rounded - 3 pins [package=THT]
  Arduino1 = Arduino
  VCC1 = Battery block 9V
  Componente1 = Triple Axis Accelerometer Breakout - ADXL335

nets:
  N1: R1.pin_0, J10.pin1, Arduino1.+5V
  N2: R1.pin_1, Arduino1.A3
  N3: R2.Pin_0, Arduino1.D13
  N4: R2.Pin_1, LED1.anode
  N5: R3.Pin_0, Arduino1.D12
  N6: R3.Pin_1, LED3.anode
  N7: R4.Pin_0, Arduino1.D11
  N8: R4.Pin_1, LED4.anode
  N9: R5.Pin_0, Arduino1.D10
  N10: R5.Pin_1, LED5.anode
  N11: R6.Pin_0, Arduino1.D9
  N12: R6.Pin_1, LED6.anode
  N13: R7.Pin_0, Arduino1.D8
  N14: R7.Pin_1, LED7.anode
  GND: LED1.cathode, LED3.cathode, LED4.cathode, LED5.cathode, LED6.cathode, LED7.cathode, LED8.cathode, LED9.cathode, Arduino1.GND, VCC1.-, Componente1.GND
  N15: R8.Pin_0, Arduino1.D7
  N16: R8.Pin_1, LED8.anode
  N17: R9.Pin_0, Arduino1.D6
  N18: R9.Pin_1, LED9.anode
  GND_2: DC_Power1.GND
  N19: J10.pin2, Componente1.VCC
  N20: J10.pin3, Arduino1.3V3
  N21: Arduino1.VIN, VCC1.+
  N22: Arduino1.A0, Componente1.XOUT
  N23: Arduino1.A1, Componente1.YOUT
  N24: Arduino1.A2, Componente1.ZOUT

notes:
  POV - Malabaris
  0.4
  Ver.:
